# Fritzing sketch schematic (saved by Fritzing 0.9.9b)
breadboards: 1

parts:
  Squix1 = OLED 0.96" 128x64 I2C SSD1306
  U1 = NodeMCU V1.0
  THERMO1 = MAX31855 Breakout Board with Thermocouple
  Mod1 = KY-019 5V Relay Module [package="Breakout board"]
  R4 = Resistor [tolerance=±5% power=0.25 resistance=10000 package=THT]
  R2 = Trimmer Potentiometer [maximum_resistance=10kΩ package=THT]
  R1 = Resistor [tolerance=±5% resistance=100000 package="2512 [SMD]"]
  R3 = Resistor [tolerance=±5% resistance=15000 package="0603 [SMD]"]
  J1 = Camdenboss CTB0158-2 [part_number=CTB0158-2 package=THT]
  J2 = Camdenboss CTB0158-2 [part_number=CTB0158-2 package=THT]
  J3 = Camdenboss CTB0158-2 [part_number=CTB0158-2 package=THT]
  J4 = Camdenboss CTB0158-2 [part_number=CTB0158-2 package=THT]
  SCW05B-1 = SCW05B-05

nets:
  VCC: Squix1.VCC, U1.3V3, THERMO1.Vin, Mod1.+, SCW05B-1.Vin_-, SCW05B-1.Vout_+
  GND: Squix1.GND, U1.GND, THERMO1.GND, Mod1.-, R4.Pin_0, R3.Pin_1, J1.pin1, SCW05B-1.GND
  N1: Squix1.SCL, U1.D2
  N2: Squix1.SCA, U1.D1
  N3: U1.D0, Mod1.S
  N4: U1.D5, THERMO1.CLK
  N5: U1.D6, THERMO1.DO
  N6: U1.D8, THERMO1.CS, R4.Pin_1
  N7: U1.A0, R2.wiper
  N8: Mod1.NC, J4.pin1
  N9: Mod1.Common, J2.pin2
  N10: Mod1.NO, J3.pin2
  N11: R2.leg1, R1.Pin_1
  N12: R2.leg2, R3.Pin_0
  N13: R1.Pin_0, J1.pin2, SCW05B-1.Vin_+
  N14: J2.pin1, J3.pin1, J4.pin2

notes:
  Voltage input from battery
  Thermocouple is taped to top of relay
  Output to HPP on front of Yeti (pretend this is a Power Pole connector)
  Controller will not boot without this resistor if max31855 is connected
  Input from primary source (solar)
  Input from auxillary source (AC power supply)

custom parts:
  NodeMCU V1.0: ESP8266 based NodeMCU
  KY-019 5V Relay Module: KY-019 5V Relay module, used to control AC circuits. (Special thanks to vanepp for fixing the PCB holes and other errors)
